// Logisim project ALU.circ as structural Verilog: 1 circuit, main circuit ALU
module ALU (
  input  Cin,
  input  [7:0] A,
  input  [7:0] B,
  input  [7:0] Multi_In,
  input  [2:0] Shift,
  input  [2:0] in_6,
  output [7:0] out_7,
  output Cout,
  output [7:0] Multi_Out
);

  wire adder_1_cout, demultiplexer_1_out1, demultiplexer_1_out2, demultiplexer_1_out3, demultiplexer_1_out4,
       demultiplexer_1_out5, demultiplexer_1_out6, demultiplexer_1_out7, subtractor_1_bout;
  wire [7:0] adder_1_out, and_1_out, multiplier_1_cout, multiplier_1_out, not_1_out, or_1_out, shifter_1_out,
       subtractor_1_out;

  assign not_1_out = ~A;  // NOT_Gate not_1, 8 bits wide
  Multiplier multiplier_1 (.a(A), .b(B), .out(multiplier_1_out), .cin(Multi_In), .cout(multiplier_1_cout));
  Shifter shifter_1 (.in(A), .\dist (Shift), .out(shifter_1_out));
  assign and_1_out = A & B;  // AND_Gate and_1, 8 bits wide
  assign or_1_out = A | B;  // OR_Gate or_1, 8 bits wide
  assign out_7 = demultiplexer_1_out2 ? or_1_out : 8'bz;  // Controlled_Buffer controlled_buffer_1
  assign out_7 = demultiplexer_1_out1 ? not_1_out : 8'bz;  // Controlled_Buffer controlled_buffer_2
  Subtractor subtractor_1 (.a(A), .b(B), .out(subtractor_1_out), .bin(Cin), .bout(subtractor_1_bout));
  assign Multi_Out = demultiplexer_1_out5 ? multiplier_1_cout : 8'bz;  // Controlled_Buffer controlled_buffer_3
  assign out_7 = demultiplexer_1_out4 ? shifter_1_out : 8'bz;  // Controlled_Buffer controlled_buffer_4
  assign out_7 = demultiplexer_1_out3 ? and_1_out : 8'bz;  // Controlled_Buffer controlled_buffer_5
  assign out_7 = demultiplexer_1_out7 ? adder_1_out : 8'bz;  // Controlled_Buffer controlled_buffer_6
  Adder adder_1 (.a(A), .b(B), .out(adder_1_out), .cin(Cin), .cout(adder_1_cout));
  assign Cout = demultiplexer_1_out7 ? adder_1_cout : 1'bz;  // Controlled_Buffer controlled_buffer_7
  assign out_7 = demultiplexer_1_out6 ? subtractor_1_out : 8'bz;  // Controlled_Buffer controlled_buffer_8
  assign Cout = demultiplexer_1_out6 ? subtractor_1_bout : 1'bz;  // Controlled_Buffer controlled_buffer_9
  assign out_7 = demultiplexer_1_out5 ? multiplier_1_out : 8'bz;  // Controlled_Buffer controlled_buffer_10
  Demultiplexer #(.select(3)) demultiplexer_1 (
    .out1(demultiplexer_1_out1), .out2(demultiplexer_1_out2), .out3(demultiplexer_1_out3),
    .out4(demultiplexer_1_out4), .out5(demultiplexer_1_out5), .out6(demultiplexer_1_out6),
    .out7(demultiplexer_1_out7), .in(1'b1), .sel(in_6));  // open: out0
endmodule
