// Logisim project CK.circ as structural Verilog: 1 circuit, main circuit SCE
module SCE (
  input  in_1,
  output K,
  output S,
  output E
);

  wire j_k_ff_1_qn, nand_1_out;

  J_K_Flip_Flop j_k_ff_1 (.J(1'b1), .K(1'b1), .clk(in_1), .Q(K), .Qn(j_k_ff_1_qn));  // open: preset, reset
  nand nand_1 (nand_1_out, in_1, K);
  nand nand_2 (E, j_k_ff_1_qn, in_1);
  not not_1 (S, nand_1_out);
endmodule
