// Logisim project CPU.circ as structural Verilog: 1 circuit, main circuit main
module main (
  output [2:0] out_1,
  output [7:0] out_2,
  output [7:0] out_3
);

  wire alu_1_p4, alu_1_p5, alu_1_p7, alu_1_p8, controlled_buffer_11_out, controlled_buffer_13_out, cu_1_p1,
       cu_1_p2, cu_1_p7, cu_1_p8, cu_1_p9, cu_1_p10, cu_1_p11, cu_1_p12, cu_1_p13, cu_1_p15, cu_1_p16,
       cu_1_p17, cu_1_p18, cu_1_p19, cu_1_p20, cu_1_p21, cu_1_p22, cu_1_p23, cu_1_p24, cu_1_p25, cu_1_p27,
       cu_1_p28, cu_1_p29, cu_1_p30, cu_1_p31, cu_1_p32, cu_1_p35, cu_1_p36, cu_1_p37, cu_1_p38, cu_1_p39,
       cu_1_p40, cu_1_p41, cu_1_p42, cu_1_p43, cu_1_p44, cu_1_p45, not_1_out, pc_1_increment_next,
       RAM_L_increment_next, undriven_2;
  wire [7:0] ACC_q, controlled_buffer_17_out, controlled_buffer_18_out, cu_1_p14, cu_1_p26, MUL_In_q,
       pc_1_pc_out, pc_2_pc_out, R0_A_q, R1_B_q, R2_q, R3_q, R4_q, R5_q, R6_q, R7_q, ram_1_dout,
       RAM_H_pc_out, RAM_L_pc_out, rom_1_data, Stack_Pointer_pc_out, undriven;

  Register #(.trigger("high")) R0_A (.D(out_3), .en(cu_1_p9), .clk(1'b1), .Q(R0_A_q));  // open: clr
  Register #(.trigger("high")) MUL_In (.D(out_3), .en(cu_1_p2), .clk(1'b1), .Q(MUL_In_q));  // open: clr
  Register #(.trigger("high")) ACC (.D(out_2), .en(cu_1_p7), .clk(1'b1), .Q(ACC_q));  // open: clr
  Register #(.trigger("high")) R1_B (.D(out_3), .en(cu_1_p11), .clk(1'b1), .Q(R1_B_q));  // open: clr
  assign out_3 = cu_1_p10 ? R0_A_q : 8'bz;  // Controlled_Buffer controlled_buffer_1
  // ALU alu_1: pin names not known; wires that end beside it: out_3, out_2, R0_A_q, alu_1_p4, alu_1_p5, MUL_In_q, alu_1_p7, alu_1_p8, out_1
  assign out_3 = cu_1_p8 ? ACC_q : 8'bz;  // Controlled_Buffer controlled_buffer_2
  assign out_3 = cu_1_p12 ? R1_B_q : 8'bz;  // Controlled_Buffer controlled_buffer_3
  Register #(.trigger("high")) R2 (.D(out_3), .en(cu_1_p15), .clk(1'b1), .Q(R2_q));  // open: clr
  // CU cu_1: pin names not known; wires that end beside it: cu_1_p1, cu_1_p2, alu_1_p5, alu_1_p7, alu_1_p8, out_1, cu_1_p7, cu_1_p8, cu_1_p9, cu_1_p10, cu_1_p11, cu_1_p12, cu_1_p13, cu_1_p14, cu_1_p15, cu_1_p16, cu_1_p17, cu_1_p18, cu_1_p19, cu_1_p20, cu_1_p21, cu_1_p22, cu_1_p23, cu_1_p24, cu_1_p25, cu_1_p26, cu_1_p27, cu_1_p28, cu_1_p29, cu_1_p30, cu_1_p31, cu_1_p32, out_3, out_3, cu_1_p35, cu_1_p36, cu_1_p37, cu_1_p38, cu_1_p39, cu_1_p40, cu_1_p41, cu_1_p42, cu_1_p43, cu_1_p44, cu_1_p45
  Clock clock_1 (.out(cu_1_p1));
  Register #(.trigger("high")) Flags (.D(out_3), .en(cu_1_p13), .clk(1'b1), .Q(cu_1_p14));  // open: clr
  Register #(.trigger("high")) R3 (.D(out_3), .en(cu_1_p17), .clk(1'b1), .Q(R3_q));  // open: clr
  assign out_3 = cu_1_p16 ? R2_q : 8'bz;  // Controlled_Buffer controlled_buffer_4
  Register #(.trigger("high")) R4 (.D(out_3), .en(cu_1_p19), .clk(1'b1), .Q(R4_q));  // open: clr
  assign out_3 = cu_1_p18 ? R3_q : 8'bz;  // Controlled_Buffer controlled_buffer_5
  Register #(.trigger("high")) INST (.D(out_3), .en(cu_1_p23), .clk(1'b1), .Q(cu_1_p26));  // open: clr
  Register #(.trigger("high")) R5 (.D(out_3), .en(cu_1_p21), .clk(1'b1), .Q(R5_q));  // open: clr
  assign out_3 = cu_1_p20 ? R4_q : 8'bz;  // Controlled_Buffer controlled_buffer_6
  assign out_3 = cu_1_p22 ? R5_q : 8'bz;  // Controlled_Buffer controlled_buffer_7
  Register #(.trigger("high")) R6 (.D(out_3), .en(cu_1_p24), .clk(1'b1), .Q(R6_q));  // open: clr
  Register #(.trigger("high")) R7 (.D(out_3), .en(cu_1_p27), .clk(1'b1), .Q(R7_q));  // open: clr
  assign out_3 = cu_1_p25 ? R6_q : 8'bz;  // Controlled_Buffer controlled_buffer_8
  Pull_Resistor pull_resistor_1 (.node(out_3));
  assign out_3 = cu_1_p28 ? R7_q : 8'bz;  // Controlled_Buffer controlled_buffer_9
  PC Stack_Pointer (
    .CLK(cu_1_p30), .Jump_Pos(undriven), .Jump_Signal(cu_1_p31), .EN(cu_1_p32),
    .PC_OUT(Stack_Pointer_pc_out), .Increment_Next(cu_1_p29));
  assign cu_1_p30 = cu_1_p31 ? cu_1_p31 : 1'bz;  // Controlled_Buffer controlled_buffer_10
  assign controlled_buffer_11_out = cu_1_p43 ? cu_1_p43 : 1'bz;  // Controlled_Buffer controlled_buffer_11
  assign controlled_buffer_11_out = cu_1_p44 ? cu_1_p44 : 1'bz;  // Controlled_Buffer controlled_buffer_12
  assign controlled_buffer_13_out = cu_1_p45 ? cu_1_p45 : 1'bz;  // Controlled_Buffer controlled_buffer_13
  assign out_3 = cu_1_p32 ? Stack_Pointer_pc_out : 8'bz;  // Controlled_Buffer controlled_buffer_14
  Pull_Resistor pull_resistor_2 (.node(cu_1_p32));
  assign controlled_buffer_13_out = controlled_buffer_11_out ? controlled_buffer_11_out : 1'bz;  // Controlled_Buffer controlled_buffer_15
  not not_1 (not_1_out, cu_1_p32);
  PC RAM_H (
    .CLK(cu_1_p37), .Jump_Pos(undriven), .Jump_Signal(cu_1_p39), .EN(RAM_L_increment_next),
    .PC_OUT(RAM_H_pc_out));  // open: Increment_Next
  assign out_3 = cu_1_p41 ? pc_1_pc_out : 8'bz;  // Controlled_Buffer controlled_buffer_16
  PC pc_1 (
    .CLK(controlled_buffer_11_out), .Jump_Pos(out_3), .Jump_Signal(cu_1_p44), .EN(1'b1),
    .PC_OUT(pc_1_pc_out), .Increment_Next(pc_1_increment_next));
  PC pc_2 (
    .CLK(controlled_buffer_13_out), .Jump_Pos(out_3), .Jump_Signal(cu_1_p45), .EN(pc_1_increment_next),
    .PC_OUT(pc_2_pc_out));  // open: Increment_Next
  assign controlled_buffer_17_out = not_1_out ? RAM_L_pc_out : 8'bz;  // Controlled_Buffer controlled_buffer_17
  PC RAM_L (
    .CLK(cu_1_p37), .Jump_Pos(undriven), .Jump_Signal(cu_1_p38), .PC_OUT(RAM_L_pc_out),
    .Increment_Next(RAM_L_increment_next));  // open: EN
  assign controlled_buffer_18_out = not_1_out ? RAM_H_pc_out : 8'bz;  // Controlled_Buffer controlled_buffer_18
  assign out_3 = cu_1_p40 ? pc_2_pc_out : 8'bz;  // Controlled_Buffer controlled_buffer_19
  assign out_3 = cu_1_p36 ? ram_1_dout : 8'bz;  // Controlled_Buffer controlled_buffer_20
  RAM #(.addrWidth(16)) ram_1 (
    .addr({controlled_buffer_18_out, controlled_buffer_17_out}), .we(cu_1_p36), .oe(cu_1_p35),
    .clk(undriven_2), .din(out_3), .dout(ram_1_dout));
  Pull_Resistor #(.pull(1)) pull_resistor_3 (.node(controlled_buffer_17_out));
  ROM #(.addrWidth(16)) rom_1 (.addr({pc_2_pc_out, pc_1_pc_out}), .data(rom_1_data));
  assign out_3 = cu_1_p42 ? rom_1_data : 8'bz;  // Controlled_Buffer controlled_buffer_21

  // Notes on the sheet:
  //   contents of rom_1 (hex, n*v repeats v):
  //   7 6 6 84 0 0 56 57 0 0 58 85 85 86 56 44 7 44 7 44 7 44 7 44 7 44 7 44 7 44 7 44 7 44 7 44 7 44 7 44
  //   7 44 7 44 7 44 7 44 7 44 7 44 7 44 7 44 7 44 7 44 7 44 7 44 7 44 7 44 7 44 7 44 7 44 7 44 7 44 7 44
  //   7 44 7 44 7 44 7 44 7 44 7 44 7 44 7 44 7 44 7 44 7 44 7 44 7 44 7 44 7 44 7 44 7 44 7 44 7 44 7 44
  //   7 44 7 44 7 44 7 44 7 44 7 44 7 44 7 44 7 44 7 44 7 44 7 44 7 44 7 44 7 44 7 44 7 44 7 44 7 44 7 44
  //   7 44 7 44 7 44 7 44 7 44 7 44 7 44 7 44 7 44 7 44 7 44 7 44 7 44 7 44 7 44 7 44 7 44 7 44 7 44 7 44
  //   7 44 7 44 7 44 7 44 7 44 7 44 7 44 7 44 7 44 7 44 7 44 7 44 7 44 7 44 7 44 7 44 7 44 7 44 7 44 7 44
endmodule
