// Logisim project CU.circ as structural Verilog: 1 circuit, main circuit CU
module CU (
  input  Ext_Reset,
  input  Clk,
  input  [7:0] Flags,
  input  [7:0] Instruction,
  input  Mul_In,
  input  Cin,
  input  JP1,
  input  JP2,
  input  in_9,
  input  in_10,
  input  [7:0] Adress_Input,
  input  Halt_In,
  output R0_En,
  output R0_Set,
  output R1_En,
  output R1_Set,
  output R2_En,
  output R2_Set,
  output R3_En,
  output R3_Set,
  output R4_En,
  output R4_Set,
  output R5_En,
  output R5_Set,
  output R6_En,
  output R6_Set,
  output R7_En,
  output R7_Set,
  output ROM_En,
  output RAM_CLK,
  output PC_CLK,
  output Halt,
  output Cout,
  output RAM_L,
  output RAM_H,
  output PC_L,
  output ACC_En,
  output [2:0] Shift,
  output RAM_SET,
  output ACC_Set,
  output RAM_EN,
  output PC_H,
  output [7:0] Adress_Output,
  output Flag_set,
  output Inst_Set,
  output [2:0] ALU
);

  wire and_9_out, and_10_out, and_12_out, and_13_out, and_14_out, and_15_out, and_16_out, and_17_out,
       and_18_out, and_19_out, and_20_out, and_21_out, and_22_out, and_23_out, and_24_out, and_25_out,
       and_26_out, and_27_out, and_28_out, and_29_out, and_30_out, and_31_out, and_32_out, and_33_out,
       and_34_out, and_35_out, and_36_out, and_37_out, and_38_out, and_39_out, and_40_out, and_41_out,
       and_42_out, and_43_out, and_44_out, and_45_out, and_46_out, and_47_out, and_48_out, and_49_out,
       and_52_out, BRANCH, Clk_t, controlled_buffer_1_out, Decode, En, En1, En2, En_High, En_Low, INC,
       Jump_1, Jump_2, Move, not_1_out, not_2_out, not_3_out, not_4_out, not_5_out, not_6_out, not_7_out,
       not_8_out, not_9_out, not_10_out, not_11_out, not_12_out, not_13_out, not_14_out, not_15_out,
       not_16_out, not_17_out, not_18_out, not_19_out, not_20_out, not_21_out, not_22_out, not_23_out,
       not_24_out, not_25_out, not_26_out, not_27_out, not_28_out, not_29_out, not_30_out, not_31_out,
       not_32_out, not_33_out, not_34_out, not_35_out, not_36_out, not_37_out, not_38_out, not_39_out,
       or_1_out, or_2_out, or_3_out, PC_CLK_t, pull_resistor_4_node, pull_resistor_14_node,
       pull_resistor_23_node, pull_resistor_48_node, pull_resistor_49_node, pull_resistor_50_node, R0E, R0S,
       R1E, R1S, R2E, R2S, R3E, R3S, R4E, R4S, R5E, R5S, R6E, R6S, R7E, R7S, Reset, Set, Set_High, Set_Low,
       stp_1_decode, stp_1_exc1, stp_1_exc2, stp_1_fectch, stp_1_out_3, stp_1_out_4, stp_1_out_5, stp_1_pc;
  wire [7:0] register_1_q, register_2_q;

  not not_1 (not_1_out, Instruction[4]);
  not not_2 (not_2_out, Instruction[3]);
  not not_3 (not_3_out, Instruction[4]);
  not not_4 (not_4_out, Instruction[3]);
  not not_5 (not_5_out, Halt);
  assign controlled_buffer_1_out = En1 ? En1 : 1'bz;  // Controlled_Buffer controlled_buffer_1
  assign controlled_buffer_1_out = En2 ? En2 : 1'bz;  // Controlled_Buffer controlled_buffer_2
  and and_1 (R0_En, pull_resistor_14_node, R0E, controlled_buffer_1_out);
  and and_2 (R1_En, pull_resistor_14_node, R1E, controlled_buffer_1_out);
  and and_3 (R2_En, pull_resistor_14_node, R2E, controlled_buffer_1_out);
  and and_4 (R3_En, pull_resistor_14_node, R3E, controlled_buffer_1_out);
  and and_5 (R4_En, pull_resistor_14_node, R4E, controlled_buffer_1_out);
  and and_6 (R5_En, pull_resistor_14_node, R5E, controlled_buffer_1_out);
  and and_7 (R6_En, pull_resistor_14_node, R6E, controlled_buffer_1_out);
  and and_8 (R7_En, pull_resistor_14_node, R7E, controlled_buffer_1_out);
  Pull_Resistor pull_resistor_1 (.node(ROM_En));
  Pull_Resistor pull_resistor_2 (.node(ACC_En));
  Pull_Resistor pull_resistor_3 (.node(ACC_Set));
  and and_9 (and_9_out, not_1_out, not_2_out);
  and and_10 (and_10_out, not_3_out, not_4_out);
  not not_6 (not_6_out, Instruction[7]);
  not not_7 (not_7_out, Instruction[2]);
  not not_8 (not_8_out, Instruction[1]);
  not not_9 (not_9_out, Instruction[0]);
  not not_10 (not_10_out, Instruction[1]);
  not not_11 (not_11_out, Instruction[0]);
  not not_12 (not_12_out, Instruction[6]);
  not not_13 (not_13_out, Instruction[5]);
  not not_14 (not_14_out, Instruction[2]);
  not not_15 (not_15_out, Instruction[1]);
  not not_16 (not_16_out, Instruction[0]);
  Pull_Resistor pull_resistor_4 (.node(pull_resistor_4_node));
  or or_1 (or_1_out, Ext_Reset, pull_resistor_4_node);
  and and_11 (Clk_t, Clk, not_5_out);
  Pull_Resistor pull_resistor_5 (.node(controlled_buffer_1_out));
  Pull_Resistor pull_resistor_6 (.node(R0E));
  Pull_Resistor pull_resistor_7 (.node(R1E));
  Pull_Resistor pull_resistor_8 (.node(R2E));
  Pull_Resistor pull_resistor_9 (.node(R3E));
  Pull_Resistor pull_resistor_10 (.node(R4E));
  Pull_Resistor pull_resistor_11 (.node(R5E));
  Pull_Resistor pull_resistor_12 (.node(R6E));
  Pull_Resistor pull_resistor_13 (.node(R7E));
  Pull_Resistor pull_resistor_14 (.node(pull_resistor_14_node));
  assign pull_resistor_14_node = En ? En : 1'bz;  // Controlled_Buffer controlled_buffer_3
  not not_17 (not_17_out, Instruction[6]);
  not not_18 (not_18_out, Instruction[5]);
  not not_19 (not_19_out, Instruction[6]);
  not not_20 (not_20_out, Instruction[5]);
  not not_21 (not_21_out, Instruction[7]);
  not not_22 (not_22_out, Instruction[5]);
  not not_23 (not_23_out, Instruction[4]);
  not not_24 (not_24_out, Instruction[3]);
  and and_12 (and_12_out, En1, and_9_out);
  and and_13 (and_13_out, En1, and_10_out);
  not not_25 (not_25_out, Instruction[4]);
  and and_14 (and_14_out, not_6_out, Instruction[6], Instruction[5]);
  STP stp_1 (
    .Reset(or_1_out), .CLK(Clk_t), .out_3(stp_1_out_3), .out_4(stp_1_out_4), .out_5(stp_1_out_5),
    .PC(stp_1_pc), .Rst(Reset), .Fectch(stp_1_fectch), .Decode(stp_1_decode), .Exc1(stp_1_exc1),
    .Exc2(stp_1_exc2));
  Pull_Resistor pull_resistor_15 (.node(RAM_L));
  Pull_Resistor pull_resistor_16 (.node(RAM_SET));
  Pull_Resistor pull_resistor_17 (.node(RAM_EN));
  and and_15 (and_15_out, Instruction[7], not_17_out, not_18_out);
  and and_16 (and_16_out, Instruction[7], not_19_out, not_20_out);
  not not_26 (not_26_out, Instruction[7]);
  not not_27 (not_27_out, Instruction[6]);
  and and_17 (and_17_out, not_26_out, not_27_out, not_28_out);
  not not_28 (not_28_out, Instruction[5]);
  and and_18 (and_18_out, not_21_out, Instruction[6], not_22_out);
  and and_19 (and_19_out, not_23_out, not_24_out);
  and and_20 (and_20_out, Instruction[4], Instruction[3]);
  not not_29 (not_29_out, Instruction[4]);
  not not_30 (not_30_out, Instruction[3]);
  and and_21 (and_21_out, and_13_out, Move, not_25_out, Instruction[3]);
  and and_22 (and_22_out, Decode, and_14_out);
  and and_23 (and_23_out, not_7_out, not_8_out, not_9_out);
  and and_24 (and_24_out, Instruction[2], not_10_out, not_11_out);
  and and_25 (and_25_out, Instruction[7], not_12_out, not_13_out, Instruction[4], not_14_out, not_15_out, not_16_out);
  assign pull_resistor_4_node = Reset ? Reset : 1'bz;  // Controlled_Buffer controlled_buffer_4
  Pull_Resistor pull_resistor_18 (.node(Inst_Set));
  assign Inst_Set = stp_1_fectch ? stp_1_fectch : 1'bz;  // Controlled_Buffer controlled_buffer_5
  Pull_Resistor pull_resistor_19 (.node(RAM_CLK));
  Pull_Resistor pull_resistor_20 (.node(RAM_H));
  Pull_Resistor pull_resistor_21 (.node(Set_Low));
  Pull_Resistor pull_resistor_22 (.node(Set_High));
  not not_31 (not_31_out, Instruction[1]);
  and and_26 (and_26_out, Instruction[2], not_31_out, not_32_out);
  not not_32 (not_32_out, Instruction[0]);
  not not_33 (not_33_out, Instruction[0]);
  not not_34 (not_34_out, Instruction[2]);
  and and_27 (and_27_out, Decode, and_17_out);
  S_R_Flip_Flop #(.trigger("high")) s_r_ff_1 (
    .S(and_28_out), .R(PC_CLK), .clk(Clk_t), .Q(Move));  // open: reset, Qn, preset
  and and_28 (and_28_out, Decode, and_18_out);
  or or_2 (or_2_out, and_19_out, and_20_out);
  and and_29 (and_29_out, and_12_out, Move, not_29_out, not_30_out);
  Decoder #(.disabled("Z"), .select(3), .tristate("true")) decoder_1 (
    .out0(R0S), .out1(R1S), .out2(R2S), .out3(R3S), .out4(R4S), .out5(R5S), .out6(R6S), .out7(R7S),
    .sel({Instruction[0], Instruction[1], Instruction[2]}), .en(and_29_out));
  Decoder #(.disabled("Z"), .select(3), .tristate("true")) decoder_2 (
    .out0(R0E), .out1(R1E), .out2(R2E), .out3(R3E), .out4(R4E), .out5(R5E), .out6(R6E), .out7(R7E),
    .sel({Instruction[0], Instruction[1], Instruction[2]}), .en(and_21_out));
  S_R_Flip_Flop #(.trigger("high")) s_r_ff_2 (
    .S(and_22_out), .R(pull_resistor_23_node), .clk(Clk_t), .Q(BRANCH), .reset(Reset));  // open: Qn, preset
  Pull_Resistor pull_resistor_23 (.node(pull_resistor_23_node));
  and and_30 (and_30_out, BRANCH, and_23_out);
  and and_31 (and_31_out, BRANCH, and_24_out);
  and and_32 (and_32_out, Decode, and_25_out);
  Pull_Resistor pull_resistor_24 (.node(Decode));
  assign Decode = stp_1_decode ? stp_1_decode : 1'bz;  // Controlled_Buffer controlled_buffer_6
  Register #(.trigger("high")) register_1 (
    .D(Adress_Input), .en(Set_Low), .clk(Set_Low), .Q(register_1_q));  // open: clr
  Register #(.trigger("high")) register_2 (
    .D(Adress_Input), .en(Set_High), .clk(Set_High), .Q(register_2_q));  // open: clr
  assign ROM_En = Inst_Set ? Inst_Set : 1'bz;  // Controlled_Buffer controlled_buffer_7
  and and_33 (and_33_out, and_15_out, and_26_out);
  and and_34 (and_34_out, and_16_out, and_35_out);
  and and_35 (and_35_out, not_33_out, Instruction[1], not_34_out);
  S_R_Flip_Flop #(.trigger("high")) s_r_ff_3 (
    .S(and_27_out), .R(PC_CLK), .clk(Clk_t), .Q(Set));  // open: reset, Qn, preset
  Register #(.trigger("high"), .width(3)) alu_reg (.D(Instruction[2:0]), .en(Clk_t), .clk(Set), .Q(ALU), .clr(PC_CLK));
  assign RAM_SET = and_21_out ? and_21_out : 1'bz;  // Controlled_Buffer controlled_buffer_8
  D_Flip_Flop #(.trigger("high")) d_ff_1 (.D(and_32_out), .clk(En1), .Q(Cin), .reset(Flags[6]));  // open: Qn, preset
  Pull_Resistor pull_resistor_25 (.node(En1));
  assign En1 = stp_1_exc1 ? stp_1_exc1 : 1'bz;  // Controlled_Buffer controlled_buffer_9
  assign Adress_Output = En_Low ? register_1_q : 8'bz;  // Controlled_Buffer controlled_buffer_10
  or or_3 (or_3_out, Halt_In, and_33_out);
  assign PC_CLK_t = and_34_out ? ~and_34_out : 1'bz;  // Controlled_Inverter controlled_inverter_1
  assign Reset = and_34_out ? ~and_34_out : 1'bz;  // Controlled_Inverter controlled_inverter_2
  not not_35 (not_35_out, Clk_t);
  not not_36 (not_36_out, Clk_t);
  Pull_Resistor pull_resistor_26 (.node(PC_CLK));
  Pull_Resistor pull_resistor_27 (.node(PC_L));
  Pull_Resistor pull_resistor_28 (.node(PC_H));
  assign Adress_Output = En_High ? register_2_q : 8'bz;  // Controlled_Buffer controlled_buffer_11
  Register #(.trigger("high"), .width(1)) register_3 (
    .D(or_3_out), .en(or_3_out), .clk(or_3_out), .Q(Halt));  // open: clr
  and and_36 (and_36_out, En1, Move, or_2_out);
  assign ACC_En = and_36_out ? and_36_out : 1'bz;  // Controlled_Buffer controlled_buffer_12
  and and_37 (and_37_out, and_30_out, not_35_out);
  and and_38 (and_38_out, and_30_out, not_36_out);
  Pull_Resistor pull_resistor_29 (.node(En2));
  assign En2 = stp_1_exc2 ? stp_1_exc2 : 1'bz;  // Controlled_Buffer controlled_buffer_13
  and and_39 (and_39_out, En1, and_37_out);
  and and_40 (and_40_out, and_37_out, En2);
  Pull_Resistor pull_resistor_30 (.node(INC));
  assign INC = stp_1_out_3 ? stp_1_out_3 : 1'bz;  // Controlled_Buffer controlled_buffer_14
  Pull_Resistor pull_resistor_31 (.node(Halt));
  Pull_Resistor pull_resistor_32 (.node(JP1));
  Pull_Resistor pull_resistor_33 (.node(JP2));
  and and_41 (and_41_out, Instruction[4], Instruction[3]);
  assign ROM_En = and_39_out ? and_39_out : 1'bz;  // Controlled_Buffer controlled_buffer_15
  assign PC_CLK = and_39_out ? and_39_out : 1'bz;  // Controlled_Buffer controlled_buffer_16
  assign ROM_En = and_40_out ? and_40_out : 1'bz;  // Controlled_Buffer controlled_buffer_17
  assign PC_CLK = and_40_out ? and_40_out : 1'bz;  // Controlled_Buffer controlled_buffer_18
  assign Set_Low = and_39_out ? and_39_out : 1'bz;  // Controlled_Buffer controlled_buffer_19
  assign Set_High = and_40_out ? and_40_out : 1'bz;  // Controlled_Buffer controlled_buffer_20
  and and_42 (and_42_out, Jump_1, and_38_out);
  and and_43 (and_43_out, and_38_out, Jump_2);
  assign PC_H = and_43_out ? and_43_out : 1'bz;  // Controlled_Buffer controlled_buffer_21
  assign En_High = and_43_out ? and_43_out : 1'bz;  // Controlled_Buffer controlled_buffer_22
  Pull_Resistor pull_resistor_34 (.node(Jump_1));
  assign Jump_1 = stp_1_out_4 ? stp_1_out_4 : 1'bz;  // Controlled_Buffer controlled_buffer_23
  and and_44 (and_44_out, En1, Set);
  and and_45 (and_45_out, En2, Set);
  and and_46 (and_46_out, Instruction[4], Instruction[3]);
  and and_47 (and_47_out, En1, and_41_out);
  Pull_Resistor pull_resistor_35 (.node(En_Low));
  assign En_Low = and_42_out ? and_42_out : 1'bz;  // Controlled_Buffer controlled_buffer_24
  assign PC_L = and_42_out ? and_42_out : 1'bz;  // Controlled_Buffer controlled_buffer_25
  Pull_Resistor pull_resistor_36 (.node(En_High));
  assign PC_CLK = PC_CLK_t ? PC_CLK_t : 1'bz;  // Controlled_Buffer controlled_buffer_26
  assign ACC_Set = and_44_out ? and_44_out : 1'bz;  // Controlled_Buffer controlled_buffer_27
  assign ACC_En = and_45_out ? and_45_out : 1'bz;  // Controlled_Buffer controlled_buffer_28
  assign R0S = and_45_out ? and_45_out : 1'bz;  // Controlled_Buffer controlled_buffer_29
  S_R_Flip_Flop #(.trigger("high")) s_r_ff_4 (
    .S(RAM_SET), .R(PC_CLK), .clk(Clk_t), .Q(RAM_CLK));  // open: reset, Qn, preset
  and and_48 (and_48_out, En1, and_46_out);
  not not_37 (not_37_out, Instruction[3]);
  not not_38 (not_38_out, Instruction[3]);
  Pull_Resistor pull_resistor_37 (.node(Jump_2));
  assign Jump_2 = stp_1_out_5 ? stp_1_out_5 : 1'bz;  // Controlled_Buffer controlled_buffer_30
  Pull_Resistor pull_resistor_38 (.node(R0S));
  Pull_Resistor pull_resistor_39 (.node(R1S));
  Pull_Resistor pull_resistor_40 (.node(R2S));
  Pull_Resistor pull_resistor_41 (.node(R3S));
  Pull_Resistor pull_resistor_42 (.node(R4S));
  Pull_Resistor pull_resistor_43 (.node(R5S));
  Pull_Resistor pull_resistor_44 (.node(R6S));
  Pull_Resistor pull_resistor_45 (.node(R7S));
  Pull_Resistor pull_resistor_46 (.node(Mul_In));
  Pull_Resistor pull_resistor_47 (.node(Cin));
  and and_49 (and_49_out, and_47_out, Move, Instruction[4], not_37_out);
  Decoder #(.disabled("Z"), .select(3), .tristate("true")) decoder_3 (
    .out0(R0S), .out1(R1S), .out2(R2S), .out3(R3S), .out4(R4S), .out5(R5S), .out6(R6S), .out7(R7S),
    .sel({Instruction[0], Instruction[1], Instruction[2]}), .en(and_49_out));
  and and_50 (RAM_EN, and_47_out, Move, Instruction[4], not_38_out);
  Pull_Resistor pull_resistor_48 (.node(pull_resistor_48_node));
  assign pull_resistor_48_node = stp_1_pc ? stp_1_pc : 1'bz;  // Controlled_Buffer controlled_buffer_31
  not not_39 (not_39_out, BRANCH);
  and and_51 (PC_CLK_t, pull_resistor_48_node, not_39_out);
  Pull_Resistor pull_resistor_49 (.node(pull_resistor_49_node));
  assign pull_resistor_49_node = En1 ? En1 : 1'bz;  // Controlled_Buffer controlled_buffer_32
  assign pull_resistor_49_node = En2 ? En2 : 1'bz;  // Controlled_Buffer controlled_buffer_33
  Pull_Resistor pull_resistor_50 (.node(pull_resistor_50_node));
  assign pull_resistor_50_node = Set ? Set : 1'bz;  // Controlled_Buffer controlled_buffer_34
  assign pull_resistor_50_node = Move ? Move : 1'bz;  // Controlled_Buffer controlled_buffer_35
  Pull_Resistor pull_resistor_51 (.node(Flag_set));
  and and_52 (and_52_out, and_48_out, Move, Instruction[4], Instruction[3]);
  assign RAM_SET = and_52_out ? and_52_out : 1'bz;  // Controlled_Buffer controlled_buffer_36
  and and_53 (R0_Set, pull_resistor_50_node, R0S, pull_resistor_49_node);
  and and_54 (R1_Set, pull_resistor_50_node, R1S, pull_resistor_49_node);
  and and_55 (R2_Set, pull_resistor_50_node, R2S, pull_resistor_49_node);
  and and_56 (R3_Set, pull_resistor_50_node, R3S, pull_resistor_49_node);
  and and_57 (R4_Set, pull_resistor_50_node, R4S, pull_resistor_49_node);
  and and_58 (R5_Set, pull_resistor_50_node, R5S, pull_resistor_49_node);
  and and_59 (R6_Set, pull_resistor_50_node, R6S, pull_resistor_49_node);
  and and_60 (R7_Set, pull_resistor_50_node, R7S, pull_resistor_49_node);

  assign Cout = Flags[6];
  assign Flags[7] = Cin;

  // Other names for the same wires on the sheet: I2 = Instruction[2]; I1 = Instruction[1]; I0 = Instruction[0];
  //   Fetch = Inst_Set; CMP = Flags[4]; Zero = Flags[5]; I3 = Instruction[3]; I4 = Instruction[4];
  //   I5 = Instruction[5]; I6 = Instruction[6]; I7 = Instruction[7]; PC_H_IN = in_10; PC_INC = PC_CLK; PC_L_IN = in_9;
  //   RAM_INC = RAM_CLK; Execute = En1; Set1 = En1; Execute_S = En2; Set2 = En2; Set_Flag = Flag_set

  // Notes on the sheet:
  //   MEM
  //   Temp Adress Storage
  //   Fetch Logic
  //   ROM >ENABLE
  //   INST-REG > SET
  //   ALU LOGIC
  //   010 XX XXX
  //   RET : 011XX111 
  //   HALT Logic    100 XX 100 
  //   NOP LOGIC     100XX101 
  //   ADD A,B  000 XX AAA
  //   MOVE ACC to Rx     010 00 Addr
  //   MOVE RX to RAM 010 01 RX
  //   BRANCH LOGIC 011 XX ABC 
  //   JUMP to Addr: JMP 011 XX 000 
  //   Decrement /Increment   100X1000 for branch Instruction's
  //   PC_INC
  //   Clk Once
  //   POP Ram to RX    010 10 RX
  //   PUSH ACC to Ram 010 11 000
  //   Flags
endmodule
