// Logisim project PC.circ as structural Verilog: 1 circuit, main circuit PC
module PC (
  input  CLK,
  input  [7:0] Jump_Pos,
  input  Jump_Signal,
  input  EN,
  output [7:0] PC_OUT,
  output Increment_Next
);

  wire n74161_1_pin1, n74161_1_pin15, not_1_out;

  not not_1 (not_1_out, Jump_Signal);
  _74161 u_74161_1 (
    .pin1(n74161_1_pin1), .pin2(CLK), .pin3(Jump_Pos[0]), .pin4(Jump_Pos[1]), .pin5(Jump_Pos[2]),
    .pin6(Jump_Pos[3]), .pin7(EN), .pin15(n74161_1_pin15), .pin14(PC_OUT[0]), .pin13(PC_OUT[1]),
    .pin12(PC_OUT[2]), .pin11(PC_OUT[3]), .pin10(EN), .pin9(not_1_out));
  _74161 u_74161_2 (
    .pin1(n74161_1_pin1), .pin2(CLK), .pin3(Jump_Pos[4]), .pin4(Jump_Pos[5]), .pin5(Jump_Pos[6]),
    .pin6(Jump_Pos[7]), .pin7(EN), .pin15(Increment_Next), .pin14(PC_OUT[4]), .pin13(PC_OUT[5]),
    .pin12(PC_OUT[6]), .pin11(PC_OUT[7]), .pin10(n74161_1_pin15), .pin9(not_1_out));
endmodule
