// Logisim project STP.circ as structural Verilog: 1 circuit, main circuit STP
module STP (
  input  Reset,
  input  CLK,
  output out_3,
  output out_4,
  output out_5,
  output PC,
  output Rst,
  output Fectch,
  output Decode,
  output Exc1,
  output Exc2
);

  wire d_ff_1_q, d_ff_2_q, d_ff_3_q, d_ff_4_q, d_ff_5_q, d_ff_6_q, d_ff_7_q, d_ff_8_q, d_ff_9_q, d_ff_10_q,
       d_ff_11_q, d_ff_12_q, d_ff_13_q, d_ff_14_q, d_ff_15_q, not_1_out, not_2_out, not_3_out, not_4_out,
       not_5_out, not_6_out, not_7_out, not_8_out, not_9_out, not_10_out, or_2_out, or_3_out;

  not not_1 (not_1_out, Reset);
  not not_2 (not_2_out, CLK);
  or or_1 (Fectch, Reset, not_3_out);
  D_Flip_Flop #(.trigger("high")) d_ff_1 (.D(not_1_out), .clk(or_2_out), .Q(d_ff_1_q));  // open: Qn, preset, reset
  or or_2 (or_2_out, not_2_out, Reset);
  or or_3 (or_3_out, Reset, CLK);
  not not_3 (not_3_out, d_ff_2_q);
  D_Flip_Flop #(.trigger("high")) d_ff_2 (.D(d_ff_1_q), .clk(or_3_out), .Q(d_ff_2_q));  // open: Qn, preset, reset
  D_Flip_Flop #(.trigger("high")) d_ff_3 (.D(d_ff_2_q), .clk(or_2_out), .Q(d_ff_3_q));  // open: Qn, preset, reset
  and and_1 (Decode, d_ff_2_q, not_4_out);
  not not_4 (not_4_out, d_ff_4_q);
  D_Flip_Flop #(.trigger("high")) d_ff_4 (.D(d_ff_3_q), .clk(or_3_out), .Q(d_ff_4_q));  // open: Qn, preset, reset
  and and_2 (Exc1, d_ff_4_q, not_5_out);
  D_Flip_Flop #(.trigger("high")) d_ff_5 (.D(d_ff_4_q), .clk(or_2_out), .Q(d_ff_5_q));  // open: Qn, preset, reset
  not not_5 (not_5_out, d_ff_6_q);
  D_Flip_Flop #(.trigger("high")) d_ff_6 (.D(d_ff_5_q), .clk(or_3_out), .Q(d_ff_6_q));  // open: Qn, preset, reset
  D_Flip_Flop #(.trigger("high")) d_ff_7 (.D(d_ff_6_q), .clk(or_2_out), .Q(d_ff_7_q));  // open: Qn, preset, reset
  and and_3 (Exc2, d_ff_6_q, not_6_out);
  not not_6 (not_6_out, d_ff_8_q);
  D_Flip_Flop #(.trigger("high")) d_ff_8 (.D(d_ff_7_q), .clk(or_3_out), .Q(d_ff_8_q));  // open: Qn, preset, reset
  D_Flip_Flop #(.trigger("high")) d_ff_9 (.D(d_ff_8_q), .clk(or_2_out), .Q(d_ff_9_q));  // open: Qn, preset, reset
  and and_4 (out_3, d_ff_8_q, not_7_out);
  D_Flip_Flop #(.trigger("high")) d_ff_10 (.D(d_ff_9_q), .clk(or_3_out), .Q(d_ff_10_q));  // open: Qn, preset, reset
  not not_7 (not_7_out, d_ff_10_q);
  and and_5 (out_4, d_ff_10_q, not_8_out);
  D_Flip_Flop #(.trigger("high")) d_ff_11 (.D(d_ff_10_q), .clk(or_2_out), .Q(d_ff_11_q));  // open: Qn, preset, reset
  not not_8 (not_8_out, d_ff_12_q);
  D_Flip_Flop #(.trigger("high")) d_ff_12 (.D(d_ff_11_q), .clk(or_3_out), .Q(d_ff_12_q));  // open: Qn, preset, reset
  and and_6 (out_5, d_ff_12_q, not_9_out);
  D_Flip_Flop #(.trigger("high")) d_ff_13 (.D(d_ff_12_q), .clk(or_2_out), .Q(d_ff_13_q));  // open: Qn, preset, reset
  not not_9 (not_9_out, d_ff_14_q);
  D_Flip_Flop #(.trigger("high")) d_ff_14 (.D(d_ff_13_q), .clk(or_3_out), .Q(d_ff_14_q));  // open: Qn, preset, reset
  and and_7 (PC, d_ff_14_q, not_10_out);
  D_Flip_Flop #(.trigger("high")) d_ff_15 (.D(d_ff_14_q), .clk(or_2_out), .Q(d_ff_15_q));  // open: Qn, preset, reset
  not not_10 (not_10_out, Rst);
  D_Flip_Flop #(.trigger("high")) d_ff_16 (.D(d_ff_15_q), .clk(or_3_out), .Q(Rst));  // open: Qn, preset, reset
endmodule
